# Fritzing sketch SchemaFritzing (saved by Fritzing 0.9.3b)
breadboards: 1

parts:
  ESP32 = ESP32S-HiLetgo [part_number=ESP32S-HiLetgo]
  TD-er1 = MH-Z19 CO2 sensor [part_number=MH-Z19]
  Part1 = SRF05 Ultrasonic Rangefinder
  DHT1 = DHT22 Humidity and Temperature Sensor
  R1 = Resistor [tolerance=±5% resistance=220 package=THT]
  ESP32_OLED = ESP32S-HiLetgo [part_number=ESP32S-HiLetgo]

nets:
  N1: ESP32.GPIO32, Part1.Echo
  N2: ESP32.GPIO33, Part1.Trig
  N3: ESP32.GPIO25, ESP32_OLED.GPIO25
  N4: ESP32.GPIO26, ESP32_OLED.GPIO26
  N5: ESP32.GPIO27, ESP32_OLED.GPIO27
  VIN: ESP32.VIN, TD-er1.Vin, Part1.VCC, DHT1.VDD, R1.Pin_1
  N6: ESP32.GPIO16, TD-er1.RX
  N7: ESP32.GPIO17, TD-er1.TX
  GND: ESP32.GND, TD-er1.GND, Part1.GND, DHT1.GND, ESP32_OLED.GND
  N8: DHT1.DATA, R1.Pin_0

custom parts:
  ESP32S-HiLetgo: HiLetgo ESP-WROOM-32 ESP32 ESP-32S Development Board 2.4GHz Dual-Mode WiFi + Bluetooth Dual Cores Microcontroller The ESP32 integrated with Antenna switches, RF Balun, power amplifiers, low-noise amplifiers, filters, and management modules, and the entire solution occupies the least area of PCB. 2.4 GHz Wi-Fi plus Bluetooth dual-mode chip, with TSMC Ultra-low power consumption 40nm technology,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
